# Fritzing sketch MIDI 8 Sequencer V1.01 (saved by Fritzing 0.9.10b)
circuit board: 12.3881cm x 9.30326cm

parts:
  ARDUINO = Arduino Nano (Rev3.0) [part_number=Arduino]
  C1 = Electrolytic Capacitor [capacitance=1µF voltage=35V package="100 mil [THT, electrolytic]"]
  C2 = Electrolytic Capacitor [capacitance=1µF voltage=35V package="100 mil [THT, electrolytic]"]
  IC1 = 6N137 [part_number=6N137 package="DIP (Dual Inline) [THT]"]
  D9 = Rectifier Diode [part_number=1N4148]
  Rx1 = Resistor [tolerance=±5% power=0.25 resistance=220 package=THT]
  Rx2 = Resistor [tolerance=±5% power=0.25 resistance=220 package=THT]
  Rx3 = Resistor [tolerance=±5% power=0.25 resistance=4.7k package=THT]
  D1 = Rectifier Diode [part_number=1N4148]
  D2 = Rectifier Diode [part_number=1N4148]
  P2 = Alpha Potentiometer Thonk [package=THT]
  D3 = Rectifier Diode [part_number=1N4148]
  P3 = Alpha Potentiometer Thonk [package=THT]
  D4 = Rectifier Diode [part_number=1N4148]
  P4 = Alpha Potentiometer Thonk [package=THT]
  D5 = Rectifier Diode [part_number=1N4148]
  P5 = Alpha Potentiometer Thonk [package=THT]
  D6 = Rectifier Diode [part_number=1N4148]
  P6 = Alpha Potentiometer Thonk [package=THT]
  D7 = Rectifier Diode [part_number=1N4148]
  P7 = Alpha Potentiometer Thonk [package=THT]
  D8 = Rectifier Diode [part_number=1N4148]
  P8 = Alpha Potentiometer Thonk [package=THT]
  R1 = Resistor [tolerance=±5% power=0.25 resistance=1k package=THT]
  L1 = LED - 3mm [color="Red (633nm)" current=0.030 package="3 mm [THT]"]
  R2 = Resistor [tolerance=±5% power=0.25 resistance=1k package=THT]
  L2 = LED - 3mm [color="Red (633nm)" current=0.030 package="3 mm [THT]"]
  R3 = Resistor [tolerance=±5% power=0.25 resistance=1k package=THT]
  L3 = LED - 3mm [color="Red (633nm)" current=0.030 package="3 mm [THT]"]
  R4 = Resistor [tolerance=±5% power=0.25 resistance=1k package=THT]
  L4 = LED - 3mm [color="Red (633nm)" current=0.030 package="3 mm [THT]"]
  R5 = Resistor [tolerance=±5% power=0.25 resistance=1k package=THT]
  L5 = LED - 3mm [color="Red (633nm)" current=0.030 package="3 mm [THT]"]
  R6 = Resistor [tolerance=±5% power=0.25 resistance=1k package=THT]
  L6 = LED - 3mm [color="Red (633nm)" current=0.030 package="3 mm [THT]"]
  R7 = Resistor [tolerance=±5% power=0.25 resistance=1k package=THT]
  L7 = LED - 3mm [color="Red (633nm)" current=0.030 package="3 mm [THT]"]
  R8 = Resistor [tolerance=±5% power=0.25 resistance=1k package=THT]
  L8 = LED - 3mm [color="Red (633nm)" current=0.030 package="3 mm [THT]"]
  STEPS = Alpha Potentiometer Thonk [package=THT]
  CLOCK_DIVISION = Alpha Potentiometer Thonk [package=THT]
  12V = Power plug
  P1 = Alpha Potentiometer Thonk [package=THT]
  P16 = Alpha Potentiometer Thonk [package=THT]
  P15 = Alpha Potentiometer Thonk [package=THT]
  P14 = Alpha Potentiometer Thonk [package=THT]
  P13 = Alpha Potentiometer Thonk [package=THT]
  P12 = Alpha Potentiometer Thonk [package=THT]
  P11 = Alpha Potentiometer Thonk [package=THT]
  P10 = Alpha Potentiometer Thonk [package=THT]
  P9 = Alpha Potentiometer Thonk [package=THT]
  D10 = Rectifier Diode [part_number=1N4148]
  D11 = Rectifier Diode [part_number=1N4148]
  D12 = Rectifier Diode [part_number=1N4148]
  D13 = Rectifier Diode [part_number=1N4148]
  D14 = Rectifier Diode [part_number=1N4148]
  D15 = Rectifier Diode [part_number=1N4148]
  D16 = Rectifier Diode [part_number=1N4148]
  D17 = Rectifier Diode [part_number=1N4148]
  S1 = Pushbutton [package="[THT]"]
  R9 = Resistor [tolerance=±5% power=0.25 resistance=100k package=THT]
  R10 = Resistor [tolerance=±5% power=0.25 resistance=100k package=THT]
  R11 = Resistor [tolerance=±5% power=0.25 resistance=100k package=THT]
  R12 = Resistor [tolerance=±5% power=0.25 resistance=100k package=THT]
  IC1_2 = TL072 [part_number=TL072 package="DIP (Dual Inline) [THT]"]
  IC1_PWR = TL072 [package="DIP (Dual Inline) [THT]"]
  IC1_A = TL072 [package="DIP (Dual Inline) [THT]"]
  IC1_B = TL072 [package="DIP (Dual Inline) [THT]"]
  R13 = Resistor [tolerance=±5% power=0.25 resistance=1k package=THT]
  R14 = Resistor [tolerance=±5% power=0.25 resistance=1k package=THT]
  C3 = Ceramic Capacitor [capacitance=100nF voltage=35V package="100 mil [THT, multilayer]"]
  VELOCITY = PJ302M [package=THT]
  PITCH = PJ302M [package=THT]
  V/2 = female pin header, 2 pins [form="♀ (female)"]
  P/2 = female pin header, 2 pins [form="♀ (female)"]
  MIDI_IN = MIDI_CONN_FEMALE_SUPPORT [package=din_5_female_support]
  78L05 = 78L05 [package="TO92 [THT]"]

nets:
  N1: ARDUINO.D0/RX, IC1.pin6, Rx2.Pin_0
  GND: ARDUINO.GND, C1.-, C2.-, IC1.pin5, Rx3.Pin_0, P2.Out, P3.Out, P4.Out, P5.Out, P6.Out, P7.Out, P8.Out, L1.cathode, L2.cathode, L3.cathode, L4.cathode, L5.cathode, L6.cathode, L7.cathode, L8.cathode, STEPS.Out, CLOCK_DIVISION.Out, 12V.GND, P1.Out, P16.Out, P15.Out, P14.Out, P13.Out, P12.Out, P11.Out, P10.Out, P9.Out, S1.Pin_3, S1.Pin_4, R10.Pin_0, R12.Pin_0, IC1_2.connector3, IC1_PWR.pin4, C3.0, VELOCITY.Pin_3, PITCH.Pin_3, 78L05.2
  Step1: ARDUINO.D2, R1.Pin_1, P1.In, P9.In
  Step2: ARDUINO.D3, P2.In, R2.Pin_1, P10.In
  Step3: ARDUINO.D4, P3.In, R3.Pin_1, P11.In
  Step4: ARDUINO.D5, P4.In, R4.Pin_1, P12.In
  Step5: ARDUINO.D6, P5.In, R5.Pin_1, P13.In
  Step6: ARDUINO.D7, P6.In, R6.Pin_1, P14.In
  Step7: ARDUINO.D8, P7.In, R7.Pin_1, P15.In
  Step8: ARDUINO.D9, P8.In, R8.Pin_1, P16.In
  N2: ARDUINO.D10, S1.Pin_1, S1.Pin_2
  5V: ARDUINO.VIN, C2.+, IC1.pin8, Rx2.Pin_1, STEPS.In, CLOCK_DIVISION.In, 78L05.1
  N3: ARDUINO.A1, STEPS.Wiper
  N4: ARDUINO.A0, CLOCK_DIVISION.Wiper
  12V: C1.+, 12V.VCC, IC1_2.connector7, IC1_PWR.pin8, C3.1, 78L05.3
  N5: IC1.pin2, D9.cathode, Rx1.Pin_1
  N6: IC1.pin3, D9.anode, MIDI_IN.MIDI_IN
  N7: IC1.pin7, Rx3.Pin_1
  N8: Rx1.Pin_0, MIDI_IN.MIDI_OUT
  N9: D1.cathode, D2.cathode, D3.cathode, D4.cathode, D5.cathode, D6.cathode, D7.cathode, D8.cathode, IC1_2.connector4, IC1_B.pin5
  N10: D1.anode, P1.Wiper
  N11: D2.anode, P2.Wiper
  N12: D3.anode, P3.Wiper
  N13: D4.anode, P4.Wiper
  N14: D5.anode, P5.Wiper
  N15: D6.anode, P6.Wiper
  N16: D7.anode, P7.Wiper
  N17: D8.anode, P8.Wiper
  N18: R1.Pin_0, L1.anode
  N19: R2.Pin_0, L2.anode
  N20: R3.Pin_0, L3.anode
  N21: R4.Pin_0, L4.anode
  N22: R5.Pin_0, L5.anode
  N23: R6.Pin_0, L6.anode
  N24: R7.Pin_0, L7.anode
  N25: R8.Pin_0, L8.anode
  N26: P16.Wiper, D10.anode
  N27: P15.Wiper, D11.anode
  N28: P14.Wiper, D12.anode
  N29: P13.Wiper, D13.anode
  N30: P12.Wiper, D14.anode
  N31: P11.Wiper, D15.anode
  N32: P10.Wiper, D16.anode
  N33: P9.Wiper, D17.anode
  N34: D10.cathode, D11.cathode, D12.cathode, D13.cathode, D14.cathode, D15.cathode, D16.cathode, D17.cathode, IC1_2.connector2, IC1_A.pin3
  N35: R9.Pin_0, R10.Pin_1, IC1_2.connector5, IC1_B.pin6, P/2.pin1
  N36: R9.Pin_1, IC1_2.connector6, IC1_B.pin7, R13.Pin_0, P/2.pin2
  N37: R11.Pin_0, R12.Pin_1, IC1_2.connector1, IC1_A.pin2, V/2.pin1
  N38: R11.Pin_1, IC1_2.connector0, IC1_A.pin1, R14.Pin_0, V/2.pin2
  N39: R13.Pin_1, PITCH.Pin_1
  N40: R14.Pin_1, VELOCITY.Pin_1

notes:
  MIDI 8 Sequencer
  Nordl3
  JLCJLCJLCJLC
  USB
  NANO

custom parts:
  6N137: Single Optocoupler
  Rectifier Diode: A standard rectifier diode
  Alpha Potentiometer Thonk: Alpha Potentiometer from Thonk.
  TL072: Dual Operational Amplifier
  TL072: Dual Operational Amplifier
  TL072: Dual Operational Amplifier
  TL072: Dual Operational Amplifier
  PJ302M: The PJ302M is a right angled mount 3.5mm switching mono phone jack.
  78L05: 3-Terminal 100mA Positive Voltage Regulator
